// Logisim project cpu.circ as structural Verilog: 5 circuits, main circuit main
module main (
  input  [31:0] INSTRUCTION,
  input  CLOCK,
  input  Jump_En,
  input  Branch_En,
  input  TYPE_J_En,
  output [31:0] FETCH_ADDRESS,
  output [31:0] s0_Value,
  output [31:0] s1_Value,
  output [31:0] t0_Value,
  output [31:0] t1_Value,
  output [31:0] a0_Value,
  output [31:0] ra_Value,
  output [31:0] sp_Value
);

  wire _0bit, ASel, BSel, equal, I_Type, JalR_Type, main_2_p1, MEM_p1, MEMRW, PcSel, R_Type, RegWEn, S_Type,
       SB_Type, U_Type, UJ_Type;
  wire [1:0] ImmSel, WBSel;
  wire [2:0] funct3;
  wire [3:0] ALUSel;
  wire [4:0] rd, rs1, rs2;
  wire [6:0] funct7, Opcode, opcode_t;
  wire [11:0] Imme_B, Imme_I, Imme_S;
  wire [19:0] bit_extender_1_out, bit_extender_2_out, bit_extender_3_out, Imme_J, Imme_U, multiplexer_1_out;
  wire [31:0] adder_1_out, bit_extender_4_out, DataA, DataB, MEM_p6, multiplexer_2_out, multiplexer_3_out, WB;
  wire [31:1] main_2_p7;

  assign bit_extender_1_out = {{8{1'b0}}, Imme_B};  // Bit_Extender bit_extender_1
  assign bit_extender_2_out = {{8{1'b0}}, Imme_S};  // Bit_Extender bit_extender_2
  assign bit_extender_3_out = {{8{1'b0}}, Imme_I};  // Bit_Extender bit_extender_3
  // Instruction_Splitting instruction_splitting_1: pin names not known; wires that end beside it: Imme_I, INSTRUCTION, funct7, rs2, Imme_S, rs1, funct3, rd, Opcode, I_Type, Imme_B, S_Type, Imme_U, R_Type, U_Type, SB_Type, JalR_Type, Imme_J, UJ_Type
  // regfile_main main_1: pin names not known; wires that end beside it: {32{1'b0}}, PcSel, CLOCK, Imme_S, rs1, rs2, rd, WB, RegWEn, CLOCK, DataA, DataB
  Multiplexer #(.select(2), .width(20)) multiplexer_1 (
    .in0(bit_extender_1_out), .in1(bit_extender_2_out), .in2(bit_extender_3_out), .in3(Imme_J),
    .out(multiplexer_1_out), .sel(ImmSel));  // open: en
  Multiplexer #(.width(32)) multiplexer_2 (
    .in0(DataA), .in1(FETCH_ADDRESS), .out(multiplexer_2_out), .sel(ASel));  // open: en
  Multiplexer #(.width(32)) multiplexer_3 (
    .in0(DataB), .in1(bit_extender_4_out), .out(multiplexer_3_out), .sel(BSel));  // open: en
  assign bit_extender_4_out = {{12{1'b0}}, multiplexer_1_out};  // Bit_Extender bit_extender_4
  Instruction_Fetch instruction_fetch_1 (
    .Jump_En(Jump_En), .Branch_En(Branch_En), .in_3(FETCH_ADDRESS), .in_2(Imme_B), .in_1(Imme_J),
    .TYPE_J_En(TYPE_J_En), .to_PC(FETCH_ADDRESS));
  // alu_main main_2: pin names not known; wires that end beside it: main_2_p1, multiplexer_2_out, multiplexer_3_out, equal, ALUSel, CLOCK, {main_2_p7, _0bit}
  Control control_1 (
    .in_1(equal), .in_2(funct3), .in_3(funct7), .in_4(opcode_t), ._0bit(_0bit));  // open: PcSel, ImmSel, ASel, BSel, ALUSel, MEMRW, RegWEn, WBSel
  Adder #(.width(32)) adder_1 (.a(FETCH_ADDRESS), .b(32'h4), .out(adder_1_out));  // open: cin, cout
  // mem_main MEM: pin names not known; wires that end beside it: MEM_p1, {main_2_p7, _0bit}, DataB, MEMRW, CLOCK, MEM_p6, BSel, ALUSel, MEMRW, RegWEn, WBSel
  Multiplexer #(.select(2), .width(32)) multiplexer_4 (
    .in0(adder_1_out), .in1({main_2_p7, _0bit}), .in2(MEM_p6), .out(WB), .sel(WBSel));  // open: in3, en

  // Other names for the same wires on the sheet: a0[31:0] = a0_Value; clk = CLOCK; fetch_addr[31:0] = FETCH_ADDRESS;
  //   ra[31:0] = ra_Value; s0[31:0] = s0_Value; s1[31:0] = s1_Value; sp[31:0] = sp_Value; t0[31:0] = t0_Value;
  //   t1[31:0] = t1_Value

  // Notes on the sheet:
  //   Output
  //   These are outputs/inputs from run.circ
  //   Inputs
  //   Input
  //   Instruction Fetch
  //   These are DEBUG/TEST outputs from your circuit.
  //   Output
endmodule

module Instruction_Fetch (
  input  [19:0] in_1,
  input  [11:0] in_2,
  input  [31:0] in_3,
  input  Jump_En,
  input  Branch_En,
  input  TYPE_J_En,
  output [31:0] to_PC
);

  wire [31:0] adder_2_out, adder_3_out, bit_extender_1_out, bit_extender_2_out, bit_extender_3_out,
       multiplexer_1_out, multiplexer_2_out, PC_4;

  Adder #(.width(32)) adder_1 (.a(in_3), .b(32'h4), .out(PC_4));  // open: cin, cout
  assign bit_extender_1_out = {{20{in_2[11]}}, in_2};  // Bit_Extender bit_extender_1
  assign bit_extender_2_out = {{12{in_1[19]}}, in_1};  // Bit_Extender bit_extender_2
  Multiplexer #(.width(32)) multiplexer_1 (
    .in0(bit_extender_1_out), .in1(bit_extender_2_out), .out(multiplexer_1_out), .sel(TYPE_J_En));  // open: en
  Adder #(.width(32)) adder_2 (.a(PC_4), .b(multiplexer_1_out), .out(adder_2_out));  // open: cin, cout
  Multiplexer #(.width(32)) multiplexer_2 (
    .in0(PC_4), .in1(adder_2_out), .out(multiplexer_2_out), .sel(Branch_En));  // open: en
  assign bit_extender_3_out = {{12{in_1[19]}}, in_1};  // Bit_Extender bit_extender_3
  Multiplexer #(.width(32)) multiplexer_3 (
    .in0(multiplexer_2_out), .in1(adder_3_out), .out(to_PC), .sel(Jump_En));  // open: en
  Adder #(.width(32)) adder_3 (.a(bit_extender_3_out), .b(PC_4), .out(adder_3_out));  // open: cin, cout

  // Other names for the same wires on the sheet: fetch_addr[31:0] = in_3; Imme_B[11:0] = in_2; Imme_J[19:0] = in_1

  // Notes on the sheet:
  //   INPUT
  //   OUTPUT
endmodule

module Instruction_Splitting (
  input  [31:0] Instruction,
  output [11:0] Imme_B,
  output I_Type,
  output [11:0] Imme_S,
  output S_Type,
  output [19:0] Imme_U,
  output R_Tpye,
  output U_Type,
  output [11:0] Imme_I,
  output SB_Type,
  output jalr_Type,
  output [19:0] Imme_J,
  output UJ_Tpye,
  output [6:0] funct7,
  output [4:0] rs2,
  output [4:0] rs1,
  output [2:0] funct3,
  output [4:0] rd,
  output [6:0] Opcode
);

  wire demultiplexer_1_out0, demultiplexer_1_out4;

  Demultiplexer #(.select(5)) demultiplexer_1 (
    .out0(demultiplexer_1_out0), .out4(demultiplexer_1_out4), .out8(S_Type), .out12(R_Tpye), .out13(U_Type),
    .out24(SB_Type), .out25(jalr_Type), .out27(UJ_Tpye), .in(1'b1), .sel(Instruction[6:2]));  // open: out1, out2, out3, out5, out6, out7, out9, out10, out11, out14, out15, out16, out17, out18, out19, out20, out21, out22, out23, out26, out28, out29, out30, out31, en
  or or_1 (I_Type, demultiplexer_1_out0, demultiplexer_1_out4);

  assign funct3 = Instruction[14:12];
  assign funct7 = Instruction[31:25];
  assign Imme_B = {Instruction[31], Instruction[7], Instruction[30:25], Instruction[11:8]};
  assign Imme_I = Instruction[31:20];
  assign Imme_J = {Instruction[31], Instruction[19:12], Instruction[20], Instruction[30:21]};
  assign Imme_S = {Instruction[31:25], Instruction[11:7]};
  assign Imme_U = Instruction[31:12];
  assign Opcode = Instruction[6:0];
  assign rd = Instruction[11:7];
  assign rs1 = Instruction[19:15];
  assign rs2 = Instruction[24:20];

  // Notes on the sheet:
  //   TYPE R - NO IMME
endmodule

module Kill_Jump_Branch (
  input  Jump_En,
  input  Branch_En,
  output Output
);

  or or_1 (Output, Jump_En, Branch_En);
endmodule

module Control (
  input  in_1,
  input  [2:0] in_2,
  input  [6:0] in_3,
  input  [6:0] in_4,
  input  _0bit,
  output PcSel,
  output [1:0] ImmSel,
  output ASel,
  output BSel,
  output [3:0] ALUSel,
  output MEMRW,
  output RegWEn,
  output [1:0] WBSel
);

  wire and_1_out, and_3_out, and_4_out, and_5_out, and_7_out, and_8_out, and_9_out, and_10_out, and_11_out,
       and_12_out, and_13_out, and_14_out, and_15_out, comparator_1_eq, comparator_2_eq, comparator_3_eq,
       comparator_4_eq, comparator_5_eq, comparator_6_eq, comparator_7_eq, comparator_8_eq, comparator_9_eq,
       comparator_10_eq, comparator_11_eq, comparator_12_eq, comparator_13_eq, comparator_14_eq,
       comparator_15_eq, comparator_16_gt, comparator_17_eq, comparator_17_gt, comparator_18_eq,
       comparator_18_gt, comparator_19_eq, comparator_19_gt, comparator_20_eq, comparator_21_eq,
       comparator_22_eq, comparator_23_eq, comparator_24_eq, comparator_25_eq, comparator_26_eq,
       comparator_27_eq, comparator_28_eq, not_3_out, not_4_out, or_3_out;
  wire [1:0] bit_extender_1_out, bit_extender_2_out, bit_extender_16_out, bit_extender_17_out,
       bit_extender_18_out, multiplier_9_out, multiplier_10_out;
  wire [3:0] bit_extender_3_out, bit_extender_7_out, bit_extender_9_out, bit_extender_10_out,
       bit_extender_11_out, bit_extender_12_out, bit_extender_13_out, bit_extender_14_out,
       bit_extender_15_out, bit_extender_19_out, bit_extender_20_out, multiplier_1_out, multiplier_2_out,
       multiplier_3_out, multiplier_4_out, multiplier_5_out, multiplier_6_out, multiplier_7_out,
       multiplier_8_out, multiplier_11_out, multiplier_12_out, s;
  wire [6:0] bit_extender_4_out, bit_extender_5_out, bit_extender_6_out, bit_extender_8_out;

  Comparator #(.width(4), .mode("unsigned")) comparator_1 (
    .a(ALUSel), .b(4'b0110), .eq(comparator_1_eq));  // open: gt, lt
  Comparator #(.width(7), .mode("unsigned")) comparator_2 (
    .a(in_4), .b(7'b0000011), .eq(comparator_2_eq));  // open: gt, lt
  assign bit_extender_1_out = {{1{1'b0}}, comparator_2_eq};  // Bit_Extender bit_extender_1
  assign bit_extender_2_out = {{1{1'b0}}, comparator_3_eq};  // Bit_Extender bit_extender_2
  Comparator #(.width(3), .mode("unsigned")) comparator_3 (.a(in_2), .b(3'b010), .eq(comparator_3_eq));  // open: gt, lt
  Comparator #(.width(7), .mode("unsigned")) comparator_4 (
    .a(in_4), .b(7'b0100011), .eq(comparator_4_eq));  // open: gt, lt
  Comparator #(.width(7), .mode("unsigned")) comparator_5 (
    .a(in_4), .b(7'b0110011), .eq(comparator_5_eq));  // open: gt, lt
  Comparator #(.width(7), .mode("unsigned")) comparator_6 (
    .a(in_4), .b(7'b1100011), .eq(comparator_6_eq));  // open: gt, lt
  Comparator #(.width(7), .mode("unsigned")) comparator_7 (
    .a(in_4), .b(7'b1101111), .eq(comparator_7_eq));  // open: gt, lt
  Comparator #(.width(1), .mode("unsigned")) comparator_8 (.a(in_1), .b(1'b1), .eq(comparator_8_eq));  // open: gt, lt
  and and_1 (and_1_out, comparator_1_eq, _0bit);
  Comparator #(.width(3), .mode("unsigned")) comparator_9 (.a(in_2), .b(3'b000), .eq(comparator_9_eq));  // open: gt, lt
  Comparator #(.width(3), .mode("unsigned")) comparator_10 (
    .a(in_2), .b(3'b001), .eq(comparator_10_eq));  // open: gt, lt
  Comparator #(.width(3), .mode("unsigned")) comparator_11 (
    .a(in_2), .b(3'b010), .eq(comparator_11_eq));  // open: gt, lt
  Comparator #(.width(3), .mode("unsigned")) comparator_12 (
    .a(in_2), .b(3'b100), .eq(comparator_12_eq));  // open: gt, lt
  Comparator #(.width(3), .mode("unsigned")) comparator_13 (
    .a(in_2), .b(3'b101), .eq(comparator_13_eq));  // open: gt, lt
  Comparator #(.width(3), .mode("unsigned")) comparator_14 (
    .a(in_2), .b(3'b110), .eq(comparator_14_eq));  // open: gt, lt
  Comparator #(.width(3), .mode("unsigned")) comparator_15 (
    .a(in_2), .b(3'b111), .eq(comparator_15_eq));  // open: gt, lt
  and and_2 (MEMRW, comparator_4_eq, 1'b1);
  and and_3 (and_3_out, comparator_5_eq, 1'b1);
  not not_1 (BSel, and_3_out);
  and and_4 (and_4_out, comparator_6_eq, 1'b1);
  or or_1 (ASel, and_4_out, and_5_out);
  and and_5 (and_5_out, comparator_7_eq, 1'b1);
  or or_2 (PcSel, comparator_8_eq, and_5_out, and_1_out);
  assign WBSel = bit_extender_1_out & bit_extender_2_out;  // AND_Gate and_6, 2 bits wide
  and and_7 (and_7_out, comparator_9_eq, 1'b1);
  and and_8 (and_8_out, comparator_10_eq, 1'b1);
  assign bit_extender_3_out = {{3{1'b0}}, comparator_11_eq};  // Bit_Extender bit_extender_3
  and and_9 (and_9_out, comparator_12_eq, 1'b1);
  and and_10 (and_10_out, comparator_14_eq, 1'b1);
  not not_2 (RegWEn, or_3_out);
  or or_3 (or_3_out, comparator_4_eq, and_4_out);
  assign bit_extender_4_out = {{6{1'b0}}, and_7_out};  // Bit_Extender bit_extender_4
  assign bit_extender_5_out = {{6{1'b0}}, and_8_out};  // Bit_Extender bit_extender_5
  Multiplier #(.width(4)) multiplier_1 (
    .a(bit_extender_3_out), .b(4'b0110), .out(multiplier_1_out));  // open: cin, cout
  assign bit_extender_6_out = {{6{1'b0}}, and_10_out};  // Bit_Extender bit_extender_6
  assign bit_extender_7_out = {{3{1'b0}}, comparator_15_eq};  // Bit_Extender bit_extender_7
  Multiplexer #(.select(4), .width(4)) multiplexer_1 (
    .in0(4'b0000), .in1(4'b0001), .in2(4'b0010), .in3(4'b0011), .in4(4'b0100), .in5(4'b0101), .in6(4'b0110),
    .in7(4'b0111), .in8(4'b1000), .in9(4'b1001), .in10(4'b1010), .out(ALUSel), .sel(s));  // open: in11, in12, in13, in14, in15, en
  not not_3 (not_3_out, comparator_16_gt);
  Comparator #(.width(7), .mode("unsigned")) comparator_16 (
    .a(bit_extender_4_out), .b(in_3), .gt(comparator_16_gt));  // open: eq, lt
  Comparator #(.width(7), .mode("unsigned")) comparator_17 (
    .a(bit_extender_5_out), .b(in_3), .gt(comparator_17_gt), .eq(comparator_17_eq));  // open: lt
  assign bit_extender_8_out = {{6{1'b0}}, and_9_out};  // Bit_Extender bit_extender_8
  Comparator #(.width(7), .mode("unsigned")) comparator_18 (
    .a(bit_extender_8_out), .b(in_3), .gt(comparator_18_gt), .eq(comparator_18_eq));  // open: lt
  assign bit_extender_9_out = {{3{1'b0}}, comparator_13_eq};  // Bit_Extender bit_extender_9
  Comparator #(.width(7), .mode("unsigned")) comparator_19 (
    .a(bit_extender_6_out), .b(in_3), .gt(comparator_19_gt), .eq(comparator_19_eq));  // open: lt
  Multiplier #(.width(4)) multiplier_2 (
    .a(bit_extender_7_out), .b(4'b0011), .out(multiplier_2_out));  // open: cin, cout
  Comparator #(.width(1), .mode("unsigned")) comparator_20 (
    .a(comparator_9_eq), .b(comparator_16_gt), .eq(comparator_20_eq));  // open: gt, lt
  Comparator #(.width(1), .mode("unsigned")) comparator_21 (
    .a(comparator_17_gt), .b(and_8_out), .eq(comparator_21_eq));  // open: gt, lt
  Comparator #(.width(1), .mode("unsigned")) comparator_22 (
    .a(comparator_17_eq), .b(comparator_10_eq), .eq(comparator_22_eq));  // open: gt, lt
  assign bit_extender_10_out = {{3{1'b0}}, comparator_18_gt};  // Bit_Extender bit_extender_10
  assign bit_extender_11_out = {{3{1'b0}}, comparator_19_gt};  // Bit_Extender bit_extender_11
  Comparator #(.width(1), .mode("unsigned")) comparator_23 (
    .a(comparator_9_eq), .b(comparator_20_eq), .eq(comparator_23_eq));  // open: gt, lt
  Comparator #(.width(1), .mode("unsigned")) comparator_24 (
    .a(comparator_9_eq), .b(not_3_out), .eq(comparator_24_eq));  // open: gt, lt
  Multiplier #(.width(4)) multiplier_3 (
    .a(bit_extender_10_out), .b(4'b0101), .out(multiplier_3_out));  // open: cin, cout
  and and_11 (and_11_out, comparator_18_eq, comparator_12_eq);
  Multiplier #(.width(4)) multiplier_4 (
    .a(bit_extender_11_out), .b(4'b0100), .out(multiplier_4_out));  // open: cin, cout
  and and_12 (and_12_out, comparator_19_eq, comparator_14_eq);
  assign bit_extender_12_out = {{3{1'b0}}, comparator_23_eq};  // Bit_Extender bit_extender_12
  Comparator #(.width(1), .mode("unsigned")) comparator_25 (
    .a(comparator_24_eq), .b(not_3_out), .eq(comparator_25_eq));  // open: gt, lt
  and and_13 (and_13_out, and_8_out, comparator_21_eq);
  and and_14 (and_14_out, comparator_22_eq, comparator_10_eq);
  assign bit_extender_13_out = {{3{1'b0}}, and_11_out};  // Bit_Extender bit_extender_13
  assign bit_extender_14_out = {{3{1'b0}}, and_12_out};  // Bit_Extender bit_extender_14
  Comparator #(.width(7), .mode("unsigned")) comparator_26 (
    .a(in_4), .b(7'b0100011), .eq(comparator_26_eq));  // open: gt, lt
  Comparator #(.width(7), .mode("unsigned")) comparator_27 (
    .a(in_4), .b(7'b0010011), .eq(comparator_27_eq));  // open: gt, lt
  Comparator #(.width(7), .mode("unsigned")) comparator_28 (
    .a(in_4), .b(7'b1101111), .eq(comparator_28_eq));  // open: gt, lt
  not not_4 (not_4_out, comparator_23_eq);
  Multiplier #(.width(4)) multiplier_5 (
    .a(bit_extender_12_out), .b(4'b0010), .out(multiplier_5_out));  // open: cin, cout
  assign bit_extender_15_out = {{3{1'b0}}, and_13_out};  // Bit_Extender bit_extender_15
  Multiplier #(.width(4)) multiplier_6 (
    .a(bit_extender_13_out), .b(4'b1001), .out(multiplier_6_out));  // open: cin, cout
  Multiplier #(.width(4)) multiplier_7 (
    .a(bit_extender_14_out), .b(4'b1010), .out(multiplier_7_out));  // open: cin, cout
  assign bit_extender_16_out = {{1{1'b0}}, comparator_26_eq};  // Bit_Extender bit_extender_16
  assign bit_extender_17_out = {{1{1'b0}}, comparator_27_eq};  // Bit_Extender bit_extender_17
  assign bit_extender_18_out = {{1{1'b0}}, comparator_28_eq};  // Bit_Extender bit_extender_18
  and and_15 (and_15_out, not_4_out, comparator_25_eq);
  Multiplier #(.width(4)) multiplier_8 (
    .a(bit_extender_15_out), .b(4'b0000), .out(multiplier_8_out));  // open: cin, cout
  assign bit_extender_19_out = {{3{1'b0}}, and_14_out};  // Bit_Extender bit_extender_19
  Multiplier #(.width(2)) multiplier_9 (.a(bit_extender_17_out), .b(2'b10), .out(multiplier_9_out));  // open: cin, cout
  Multiplier #(.width(2)) multiplier_10 (
    .a(bit_extender_18_out), .b(2'b11), .out(multiplier_10_out));  // open: cin, cout
  assign bit_extender_20_out = {{3{1'b0}}, and_15_out};  // Bit_Extender bit_extender_20
  Multiplier #(.width(4)) multiplier_11 (
    .a(bit_extender_19_out), .b(4'b1000), .out(multiplier_11_out));  // open: cin, cout
  assign ImmSel = bit_extender_16_out | multiplier_9_out | multiplier_10_out;  // OR_Gate or_4, 2 bits wide
  Multiplier #(.width(4)) multiplier_12 (
    .a(bit_extender_20_out), .b(4'b0111), .out(multiplier_12_out));  // open: cin, cout
  assign s = multiplier_5_out | multiplier_12_out | multiplier_8_out | multiplier_11_out | multiplier_1_out | multiplier_3_out | multiplier_6_out | bit_extender_9_out | multiplier_4_out | multiplier_7_out | multiplier_2_out;  // OR_Gate or_5, 4 bits wide

  // Other names for the same wires on the sheet: equal = in_1; funct3[2:0] = in_2; funct7[6:0] = in_3;
  //   opcode[6:0] = in_4

  // Notes on the sheet:
  //   Input
  //   Output
endmodule
