// Logisim project cpu.circ as structural Verilog: 6 circuits, main circuit main
module main (
  input  [15:0] INSTRUCTION,
  input  CLOCK,
  output [15:0] FETCH_ADDRESS,
  output [15:0] s0_Value,
  output [15:0] s1_Value,
  output [15:0] s2_Value,
  output [15:0] ra_Value,
  output [15:0] sp_Value,
  output [15:0] HI_Value,
  output [15:0] LO_Value
);

  wire ALUSrc, branch, equal, extOp, j, jr, kill_1_output, lui, memToReg, memWr, mfhi, mflo, regWr, U,
       Write_HILO;
  wire [1:0] rd_u;
  wire [2:0] ALUControl, bit_extender_1_out, Funct, multiplexer_4_out, multiplexer_5_out,
       parameter_select_1_param1, parameter_select_1_param2, rd, rs, rt;
  wire [3:0] opcode;
  wire [5:0] Imme_I;
  wire [9:0] Imme_U;
  wire [15:0] bit_extender_2_out, bit_extender_3_out, bit_extender_4_out, dataToReg, inst_fetch_1_to_pc,
       main_1_p13, main_2_p5, MEM_p5, multiplexer_1_out, multiplexer_2_out, multiplexer_6_out,
       multiplexer_7_out, multiplexer_8_out, multiplexer_9_out, multiplexer_10_out, register_1_q, write_HI,
       writeBack, writeData;

  Register #(.width(16)) LO (.D(writeBack), .en(Write_HILO), .Q(LO_Value), .clk(CLOCK));  // open: clr
  Multiplexer #(.width(16), .enable("false")) multiplexer_1 (
    .in0(INSTRUCTION), .in1({16{1'b0}}), .out(multiplexer_1_out), .sel(kill_1_output));
  kill kill_1 (.j(j), .jr(jr), .branch(branch), .Output(kill_1_output));
  Multiplexer #(.width(16), .enable("false")) multiplexer_2 (
    .in0(writeBack), .in1(HI_Value), .out(multiplexer_2_out), .sel(mfhi));
  Register #(.width(16)) register_1 (.D(multiplexer_1_out), .Q(register_1_q), .clk(CLOCK));  // open: en, clr
  Register #(.width(16)) HI (.D(write_HI), .en(Write_HILO), .Q(HI_Value), .clk(CLOCK));  // open: clr
  assign bit_extender_1_out = {{1{1'b0}}, rd_u};  // Bit_Extender bit_extender_1
  Multiplexer #(.width(16), .enable("false")) multiplexer_3 (
    .in0(multiplexer_2_out), .in1(LO_Value), .out(dataToReg), .sel(mflo));
  Inst_Split inst_split_1 (
    .Instruction(register_1_q), .Opcode(opcode), .rd_u(rd_u), .rd(rd), .rs(rs), .rt(rt), .Funct(Funct),
    .Imme_I(Imme_I), .Imme_U(Imme_U));
  Multiplexer #(.width(3), .enable("false")) multiplexer_4 (
    .in0(rd), .in1(bit_extender_1_out), .out(multiplexer_4_out), .sel(U));
  assign bit_extender_2_out = {{10{1'b0}}, Imme_I};  // Bit_Extender bit_extender_2
  assign bit_extender_3_out = {{10{Imme_I[5]}}, Imme_I};  // Bit_Extender bit_extender_3
  Parameter_Select parameter_select_1 (
    .rd(rd), .rs(rs), .rt(rt), .MemWr(memWr), .jr(jr), .Param1(parameter_select_1_param1),
    .Param2(parameter_select_1_param2));
  Multiplexer #(.width(3), .enable("false")) multiplexer_5 (
    .in0(multiplexer_4_out), .in1(3'b001), .out(multiplexer_5_out), .sel(j));
  Multiplexer #(.width(16), .enable("false")) multiplexer_6 (
    .in0(bit_extender_2_out), .in1(bit_extender_3_out), .out(multiplexer_6_out), .sel(extOp));
  assign bit_extender_4_out = {{6{1'b0}}, Imme_U};  // Bit_Extender bit_extender_4
  Inst_Fetch inst_fetch_1 (
    .fetch_addr(FETCH_ADDRESS), .Imme_U(Imme_U), .Imme_I(Imme_I), .U_Enable(U), .Branch_Enable(branch),
    .j_Enable(j), .jr_Enable(jr), .to_PC(inst_fetch_1_to_pc));
  Multiplexer #(.width(16), .enable("false")) multiplexer_7 (
    .in0(multiplexer_6_out), .in1(bit_extender_4_out), .out(multiplexer_7_out), .sel(lui));
  // regfile_main main_1: pin names not known; wires that end beside it: parameter_select_1_param1, parameter_select_1_param2, multiplexer_5_out, s0_Value, dataToReg, s1_Value, regWr, s2_Value, CLOCK, ra_Value, sp_Value, writeData, main_1_p13
  Register #(.width(16)) PC (.D(inst_fetch_1_to_pc), .Q(FETCH_ADDRESS), .clk(CLOCK));  // open: en, clr
  Multiplexer #(.width(16), .enable("false")) multiplexer_8 (
    .in0(writeData), .in1(multiplexer_7_out), .out(multiplexer_8_out), .sel(ALUSrc));
  Multiplexer #(.width(16), .enable("false")) multiplexer_9 (
    .in0(main_1_p13), .in1(16'h6), .out(multiplexer_9_out), .sel(lui));
  // alu_main main_2: pin names not known; wires that end beside it: multiplexer_8_out, multiplexer_9_out, ALUControl, equal, main_2_p5, write_HI
  Control control_1 (
    .OpCode(opcode), .Funct(Funct), .Equal(equal), .ALUSrc(ALUSrc), .lui(lui), .j(j), .jr(jr), .mfhi(mfhi),
    .mflo(mflo), .MemToReg(memToReg), .MemWr(memWr), .Write_HILO(Write_HILO), .RegWr(regWr), .ExtOp(extOp),
    .Branch(branch), .ALUControl(ALUControl), .U_type(U));
  // mem_main MEM: pin names not known; wires that end beside it: main_2_p5, writeData, memWr, CLOCK, MEM_p5
  Multiplexer #(.width(16), .enable("false")) multiplexer_10 (
    .in0(main_2_p5), .in1(MEM_p5), .out(multiplexer_10_out), .sel(memToReg));
  Multiplexer #(.width(16), .enable("false")) multiplexer_11 (
    .in0(multiplexer_10_out), .in1(FETCH_ADDRESS), .out(writeBack), .sel(j));

  // Other names for the same wires on the sheet: clk = CLOCK; fetch_addr[15:0] = FETCH_ADDRESS; HI[15:0] = HI_Value;
  //   LO[15:0] = LO_Value; ra[15:0] = ra_Value; s0[15:0] = s0_Value; s1[15:0] = s1_Value; s2[15:0] = s2_Value;
  //   sp[15:0] = sp_Value

  // Notes on the sheet:
  //   Instruction Splitting
  //   Output
  //   These are outputs/inputs from run.circ
  //   Inputs
  //   Instruction Fetch
  //   These are DEBUG/TEST outputs from your circuit.
  //   Control
endmodule

module Inst_Split (
  input  [15:0] Instruction,
  output [5:0] Imme_I,
  output [9:0] Imme_U,
  output [3:0] Opcode,
  output [2:0] rd,
  output [2:0] rs,
  output [2:0] rt,
  output [2:0] Funct,
  output [1:0] rd_u
);


  assign Funct = Instruction[2:0];
  assign Imme_I = Instruction[5:0];
  assign Imme_U = Instruction[9:0];
  assign Opcode = Instruction[15:12];
  assign rd = Instruction[11:9];
  assign rd_u = Instruction[10:9];
  assign rs = Instruction[8:6];
  assign rt = Instruction[5:3];
endmodule

module kill (
  input  j,
  input  jr,
  input  branch,
  output Output
);

  or or_1 (Output, j, jr, branch);

  // Notes on the sheet:
  //   Kill Instruction
endmodule

module Inst_Fetch (
  input  [15:0] fetch_addr,
  input  [9:0] Imme_U,
  input  [5:0] Imme_I,
  input  Branch_Enable,
  input  j_Enable,
  input  jr_Enable,
  input  U_Enable,
  output [15:0] to_PC
);

  wire [15:0] adder_2_out, adder_3_out, bit_extender_1_out, bit_extender_2_out, bit_extender_3_out,
       multiplexer_1_out, multiplexer_2_out, multiplexer_3_out, PC_2;

  assign bit_extender_1_out = {{10{Imme_I[5]}}, Imme_I};  // Bit_Extender bit_extender_1
  assign bit_extender_2_out = {{6{Imme_U[9]}}, Imme_U};  // Bit_Extender bit_extender_2
  Adder #(.width(16)) adder_1 (.a(fetch_addr), .b(16'h2), .out(PC_2));  // open: cin, cout
  Adder #(.width(16)) adder_2 (.a(PC_2), .b(multiplexer_1_out), .out(adder_2_out));  // open: cin, cout
  Multiplexer #(.width(16), .enable("false")) multiplexer_1 (
    .in0(bit_extender_1_out), .in1(bit_extender_2_out), .out(multiplexer_1_out), .sel(U_Enable));
  Multiplexer #(.width(16), .enable("false")) multiplexer_2 (
    .in0(PC_2), .in1(adder_2_out), .out(multiplexer_2_out), .sel(Branch_Enable));
  assign bit_extender_3_out = {{10{Imme_I[5]}}, Imme_I};  // Bit_Extender bit_extender_3
  Multiplexer #(.width(16), .enable("false")) multiplexer_3 (
    .in0(multiplexer_2_out), .in1({PC_2[15:10], Imme_U}), .out(multiplexer_3_out), .sel(j_Enable));
  Adder #(.width(16)) adder_3 (.a(bit_extender_3_out), .b(16'h2), .out(adder_3_out));  // open: cin, cout
  Multiplexer #(.width(16), .enable("false")) multiplexer_4 (
    .in0(multiplexer_3_out), .in1(adder_3_out), .out(to_PC), .sel(jr_Enable));

  // Notes on the sheet:
  //   PC+2
endmodule

module Control (
  input  [3:0] OpCode,
  input  [2:0] Funct,
  input  Equal,
  output ALUSrc,
  output lui,
  output j,
  output jr,
  output mfhi,
  output mflo,
  output MemToReg,
  output MemWr,
  output Write_HILO,
  output RegWr,
  output ExtOp,
  output Branch,
  output [2:0] ALUControl,
  output U_type
);

  wire addi, and_1_out, and_2_out, and_3_out, and_4_out, andi, beq, bne, comparator_1_lt, comparator_2_eq,
       comparator_3_eq, or_1_out, ori, R_Type, slti;
  wire [2:0] multiplexer_1_out;

  or or_1 (or_1_out, MemWr, lui);
  Comparator #(.width(3), .mode("unsigned")) comparator_1 (
    .a(Funct), .b(3'b111), .lt(comparator_1_lt));  // open: gt, eq
  Decoder #(.select(4), .enable("false")) decoder_1 (
    .out0(R_Type), .out1(lui), .out2(j), .out3(jr), .out4(beq), .out5(bne), .out6(addi), .out7(slti),
    .out8(andi), .out9(ori), .out10(MemToReg), .out11(MemWr), .out12(mfhi), .out13(mflo), .sel(OpCode));  // open: out14, out15
  and and_1 (and_1_out, ~or_1_out, comparator_1_lt);  // AND_Gate
  or or_2 (RegWr, mfhi, and_1_out, slti, MemToReg, jr, j, ori, andi, addi, mflo);
  Comparator #(.width(4), .mode("unsigned")) comparator_2 (
    .a(OpCode), .b(4'b0000), .eq(comparator_2_eq));  // open: gt, lt
  Comparator #(.width(3), .mode("unsigned")) comparator_3 (
    .a(Funct), .b(3'b111), .eq(comparator_3_eq));  // open: gt, lt
  Multiplexer #(.select(4), .width(3), .enable("false")) multiplexer_1 (
    .in0(3'b000), .in1(3'b000), .in2(3'b000), .in3(3'b000), .in4(3'b000), .in5(3'b000), .in6(3'b010),
    .in7(3'b110), .in8(3'b011), .in9(3'b100), .in10(3'b010), .in11(3'b010), .in12(3'b000), .in13(3'b000),
    .in14(3'b000), .in15(3'b000), .out(multiplexer_1_out), .sel(OpCode));
  or or_3 (ALUSrc, lui, addi, slti, MemWr, andi, ori, MemToReg);
  or or_4 (ExtOp, MemToReg, MemWr, slti, addi);
  or or_5 (Write_HILO, lui, and_2_out);
  and and_2 (and_2_out, comparator_2_eq, comparator_3_eq);
  Multiplexer #(.width(3), .enable("false")) multiplexer_2 (
    .in0(multiplexer_1_out), .in1(Funct), .out(ALUControl), .sel(R_Type));
  and and_3 (and_3_out, beq, Equal);
  and and_4 (and_4_out, ~Equal, bne);  // AND_Gate
  or or_6 (U_type, lui, j);
  or or_7 (Branch, and_3_out, and_4_out);

  // Other names for the same wires on the sheet: lh = MemToReg; liu = lui; sh = MemWr

  // Notes on the sheet:
  //   Input
  //   U & I Types
  //   Outputs
endmodule

module Parameter_Select (
  input  [2:0] rd,
  input  [2:0] rs,
  input  [2:0] rt,
  input  MemWr,
  input  jr,
  output [2:0] Param1,
  output [2:0] Param2
);

  wire or_1_out, or_2_out;

  Multiplexer #(.width(3), .enable("false")) multiplexer_1 (.in0(rs), .in1(rd), .out(Param1), .sel(or_1_out));
  or or_1 (or_1_out, MemWr, jr);
  Multiplexer #(.width(3), .enable("false")) multiplexer_2 (.in0(rt), .in1(rs), .out(Param2), .sel(or_2_out));
  or or_2 (or_2_out, MemWr, jr);
endmodule
